# Fritzing sketch alarm clock project (saved by Fritzing 1.0.5)
breadboards: 1

parts:
  pi = Raspberry Pi Pico W
  SP2 = SPEAKER [package=pcb_mount_speaker]
  L9110h1 = DIP - 8 pins [part_number=L9110H chip_label=L9110h package="DIP (Dual Inline) [THT]"]
  Q1 = NPN-Transistor [package="TO92 [THT]"]
  DFPlayer_Mini1 = DFPlayer MINI [package="DIP (Dual Inline) [THT]"]
  M2 = OLED Mono 2.42 inch green
  Part1 = PowerBoost 500 Charger
  BAT1 = BC9VPC [package=bc9vpc]
  M3 = DC Motor [voltage_(max)=6V voltage_(min)=3V]
  U1 = LIPO-110mAh [package=lipo-110]  # not connected
  S1 = Pushbutton [package="[THT]"]

nets:
  GND: pi.pin_3, pi.pin_8, pi.pin_13, pi.pin_18, pi.pin_23, pi.pin_28, pi.pin_33, pi.pin_38, L9110h1.GND, DFPlayer_Mini1.GND#9, M2.GND, Part1.GND, BAT1.V-, S1.Pin_1, S1.Pin_2
  N1: pi.pin_15, M2.CS
  N2: pi.pin_16, M2.DC
  N3: pi.pin_17, M2.RES
  N4: pi.pin_19, M2.SCK
  N5: pi.pin_20, M2.SDA
  N6: pi.pin_21, DFPlayer_Mini1.RX
  N7: pi.pin_22, DFPlayer_Mini1.TX
  N8: pi.pin_24, L9110h1.IB
  N9: pi.pin_25, L9110h1.IA
  N10: pi.pin_26, DFPlayer_Mini1.BUSY
  N11: pi.pin_30, S1.Pin_4
  VCC: pi.pin_36, DFPlayer_Mini1.VCC, M2.VCC
  N12: pi.pin_39, Part1.5.0V
  N13: pi.pin_40, Part1.USB
  N14: SP2.+, Q1.C
  N15: SP2.-, DFPlayer_Mini1.SPK1
  N16: L9110h1.OA, M3.pin_1
  N17: L9110h1.Vcc, BAT1.V+
  N18: L9110h1.OB, M3.pin_2
  N19: Q1.E, DFPlayer_Mini1.SPK2

custom parts:
  Raspberry Pi Pico W: Raspberry Pi Pico W. Based around the RP2040 microcontroller the Pico W is a low cost microcontroller device bringing Raspberry Pi quality, cost, and easy of use to the microcontroller space. The areas marked KEEPOUT in pcb silkscreen should not have traces running through them to avoid shorts on a soldered in module!
  DIP - 8 pins: A DIP stand-in part for whatever IC you want. With 8 pins on a 300mil dual inline package (DIP) footprint.
  DFPlayer MINI: MP3 module by DFRobot.com for playing Music from an SD-Card. Supports WAV and MP3 files.
  OLED Mono 2.42 inch green: This is a 2.42 inch OLED display module of 128x64 resolution.
